# Fritzing sketch wiring (saved by Fritzing 0.9.3b)
breadboards: 1

parts:
  Деталь1 = Arduino Uno (Rev3)
  Деталь2 = RFID-RC522-v3
  ENC28J1 = ENC28J60

nets:
  N1: Деталь1.D8, Деталь2.RST
  N2: Деталь1.D9_PWM, Деталь2.SDA
  N3: Деталь1.D10_PWM/SS, ENC28J1.CS
  N4: Деталь1.D11_PWM/MOSI, Деталь2.MOSI, ENC28J1.SI
  N5: Деталь1.D12/MISO, Деталь2.MISO, Деталь2.IRQ, ENC28J1.INT, ENC28J1.SO, ENC28J1.WOL
  N6: Деталь1.D13/SCK, Деталь1.RESET, Деталь2.SCK, ENC28J1.SCK, ENC28J1.RST
  3V3: Деталь1.3V3, Деталь2.3.3V, ENC28J1.3.3
  GND: Деталь1.GND, Деталь2.GND, ENC28J1.GND

custom parts:
  RFID-RC522-v3: A simple China made RFID-RC522 Reader (6x4 cm); do check the pin labels, as this is a MFRC522 based clone.
  ENC28J60: Ethernet Module ENC28J60
